// Logisim project circuitos_lab_2.circ as structural Verilog: 15 circuits, main circuit main
module main (
);

  wire CLK, CLKCAIDA, clock_1_out, fa, fail, fb, fc, fd, fe, ff, fg, Fin, Ganar, ha, ha1, hb, hb1, hc, hc1,
       hd, hd1, he, he1, hf, hf1, hg, hg1, Hit, mod2_1_value, nvl1, nvl2, or_1_out, Reset;
  wire [1:0] movimiento;
  wire [3:0] count_fails_1_count_value, random_num_1_num_random;
  wire [5:0] count_hits_1_count_value;
  wire [15:0] cursor_1_out_3, Down, driver_1_out_2, R1, R2, R3, R4, R5, R6, R7, R8, R9, R10, R11, R12, R13,
       R14, R15;

  Clock clock_1 (.out(clock_1_out));
  or or_1 (or_1_out, Ganar, Fin);
  and and_1 (CLK, ~or_1_out, clock_1_out);  // AND_Gate
  count_hits count_hits_1 (.Reset(Reset), .clock(Hit), .Count_value(count_hits_1_count_value));
  hits hits_1 (
    .Entrada(count_hits_1_count_value), .a(ha), .b(hb), .c(hc), .d(hd), .e(he), .f(hf), .g(hg), .a1(ha1),
    .b1(hb1), .c1(hc1), .d1(hd1), .e1(he1), .f1(hf1), .g1(hg1));
  cursor cursor_1 (.reset(Reset), .Entrada(movimiento), .out_3(cursor_1_out_3));
  // Probe on random_num_1_num_random
  random_num random_num_1 (.Reset(Reset), .Clock(CLKCAIDA), .Num_random(random_num_1_num_random));
  mod2 mod2_1 (.Clock(CLKCAIDA), .Value(mod2_1_value));
  DotMatrix #(.dotshape("circle"), .inputtype("row"), .matrixcols(16), .matrixrows(16)) dotmatrix_1 (
    .row0(Down), .row1(R1), .row2(R2), .row3(R3), .row4(R4), .row5(R5), .row6(R6), .row7(R7), .row8(R8),
    .row9(R9), .row10(R10), .row11(R11), .row12(R12), .row13(R13), .row14(R14), .row15(R15));
  DotMatrix #(.dotshape("circle"), .inputtype("row"), .matrixcols(16), .matrixrows(1)) dotmatrix_2 (.row0(cursor_1_out_3));
  Joystick #(.bits(2)) joystick_1 (.x(movimiento));  // open: y
  Button button_1 (.out(Reset));
  count_fails count_fails_1 (.Reset(Reset), .CLK(fail), .Fin(Fin), .Count_value(count_fails_1_count_value));
  Driver driver_1 (.input1(random_num_1_num_random), .out_2(driver_1_out_2));
  _7_Segment_Display u_7_segment_display_1 (.g(hg1), .f(hf1), .a(ha1), .b(hb1), .e(he1), .d(hd1), .c(hc1));  // open: dp
  _7_Segment_Display u_7_segment_display_2 (.g(hg), .f(hf), .a(ha), .b(hb), .e(he), .d(hd), .c(hc));  // open: dp
  Comparador comparador_1 (.R15(R15), .cursor(cursor_1_out_3), .Hit(Hit), .Fail(fail));
  Multiplexer #(.enable("false"), .width(16)) multiplexer_1 (
    .in0(driver_1_out_2), .in1({16{1'b0}}), .out(Down), .sel(mod2_1_value));
  fails fails_1 (.Entrada(count_fails_1_count_value), .fa(fa), .fb(fb), .fc(fc), .fd(fd), .fe(fe), .ff(ff), .fg(fg));
  LED led_1 (.in(Ganar));
  _7_Segment_Display u_7_segment_display_3 (.g(fg), .f(ff), .a(fa), .b(fb), .e(fe), .d(fd), .c(fc));  // open: dp
  _7_Segment_Display u_7_segment_display_4 (.g(fg), .f(ff), .a(fa), .b(fb), .e(fe), .d(fd), .c(fc));  // open: dp
  LED led_2 (.in(Fin));
  frecuencias frecuencias_1 (.nvl2(nvl2), .nvl1(nvl1), .CLK(CLK), .salida(CLKCAIDA));
  and nivel_1 (nvl1, ha1, hb1, hc1, ~hg1, hd1, he1, hf1);  // AND_Gate
  and nivel_2 (nvl2, ~ha1, hb1, hc1, ~hd1, ~he1, ~hf1, ~hg1);  // AND_Gate
  and u_Fin (Ganar, ha1, hb1, ~hc1, hg1, hd1, he1, ~hf1);  // AND_Gate
  stars_fall stars_fall_1 (
    .Reset(Reset), .Clock(CLKCAIDA), .Down(Down), .R1(R1), .R2(R2), .R3(R3), .R4(R4), .R5(R5), .R6(R6),
    .R7(R7), .R8(R8), .R9(R9), .R10(R10), .R11(R11), .R12(R12), .R13(R13), .R14(R14), .R15(R15));

  // Other names for the same wires on the sheet: R0[15:0] = Down

  // Notes on the sheet:
  //   fin = cuando muere 7 veces
  //   ESTRELLAS CAPTURADAS
  //   Partida ganada
  //   VIDAS PERDIDAS
  //   Fin de la partida
endmodule

module movement (
  input  Reset,
  input  [1:0] Entrada,
  output out_3,
  output out_4,
  output out_5,
  output out_6,
  output out_7,
  output out_8,
  output out_9,
  output out_10,
  output out_11,
  output out_12,
  output out_13,
  output out_14,
  output out_15,
  output out_16,
  output out_17,
  output out_18
);

  wire clock_1_out;
  wire [1:0] accion;
  wire [3:0] counter_1_q;

  Joystick #(.bits(2)) joystick_1 (.x(accion));  // open: y
  Clock clock_1 (.out(clock_1_out));
  Counter #(.max('hf), .width(4)) counter_1 (
    .clr(Reset), .up(Entrada[1]), .count(Entrada[0]), .clk(clock_1_out), .Q(counter_1_q));  // open: load, D, carry
  Decoder #(.select(4)) decoder_1 (
    .out0(out_3), .out1(out_4), .out2(out_5), .out3(out_6), .out4(out_7), .out5(out_8), .out6(out_9),
    .out7(out_10), .out8(out_11), .out9(out_12), .out10(out_13), .out11(out_14), .out12(out_15),
    .out13(out_16), .out14(out_17), .out15(out_18), .sel(counter_1_q));  // open: en
  // Probe on counter_1_q
endmodule

module divisor_reloj_frecuency (
  input  nivel1,
  input  nivel2,
  input  reset,
  input  Clock,
  output CLKD2,
  output CLKD4,
  output CLKD8
);

  wire [2:0] counter_1_q;

  Counter #(.max('h7), .width(3)) counter_1 (
    .clr(reset), .up(1'b1), .count(1'b1), .clk(Clock), .Q(counter_1_q));  // open: load, D, carry
  // Probe on counter_1_q
  and and_1 (CLKD8, counter_1_q[0], counter_1_q[1], counter_1_q[2]);
  and and_2 (CLKD2, counter_1_q[0], nivel2);
  and and_3 (CLKD4, counter_1_q[0], nivel1, counter_1_q[1]);
endmodule

module cursor (
  input  reset,
  input  [1:0] Entrada,
  output [15:0] out_3
);

  movement movement_1 (
    .Reset(reset), .Entrada(Entrada), .out_3(out_3[15]), .out_4(out_3[14]), .out_5(out_3[13]),
    .out_6(out_3[12]), .out_7(out_3[11]), .out_8(out_3[10]), .out_9(out_3[9]), .out_10(out_3[8]),
    .out_11(out_3[7]), .out_12(out_3[6]), .out_13(out_3[5]), .out_14(out_3[4]), .out_15(out_3[3]),
    .out_16(out_3[2]), .out_17(out_3[1]), .out_18(out_3[0]));
endmodule

module hits (
  input  [5:0] Entrada,
  output a,
  output b,
  output c,
  output d,
  output e,
  output f,
  output g,
  output a1,
  output b1,
  output c1,
  output d1,
  output e1,
  output f1,
  output g1
);

  wire binairy_to_bcd_converter_1_p2, binairy_to_bcd_converter_1_p3;

  // Binairy_to_BCD_converter #(.binvalue(6)) binairy_to_bcd_converter_1: pin names not known; wires that end beside it: Entrada, binairy_to_bcd_converter_1_p2, binairy_to_bcd_converter_1_p3
  // BCD_to_7_Segment_decoder bcd_to_7_segment_decoder_1: pin names not known; wires that end beside it: g, e, f, d, binairy_to_bcd_converter_1_p3, a, c, b
  // BCD_to_7_Segment_decoder bcd_to_7_segment_decoder_2: pin names not known; wires that end beside it: g1, e1, f1, d1, binairy_to_bcd_converter_1_p2, a1, c1, b1
endmodule

module fails (
  input  [3:0] Entrada,
  output fa,
  output fb,
  output fc,
  output fd,
  output fe,
  output ff,
  output fg
);

  wire and_1_out, and_2_out, and_3_out, and_4_out, and_5_out, and_6_out, and_7_out, and_8_out, and_9_out,
       and_10_out, and_11_out, and_12_out, and_13_out, and_14_out, and_15_out, and_16_out, and_17_out;

  and and_1 (and_1_out, Entrada[2], Entrada[0]);
  and and_2 (and_2_out, ~Entrada[2], ~Entrada[0]);  // AND_Gate
  and and_3 (and_3_out, Entrada[1], Entrada[0]);
  and and_4 (and_4_out, ~Entrada[1], ~Entrada[0]);  // AND_Gate
  and and_5 (and_5_out, Entrada[0], Entrada[1]);
  and and_6 (and_6_out, ~Entrada[2], ~Entrada[0]);  // AND_Gate
  and and_7 (and_7_out, Entrada[1], ~Entrada[0]);  // AND_Gate
  and and_8 (and_8_out, Entrada[2], ~Entrada[1], Entrada[0]);  // AND_Gate
  and and_9 (and_9_out, ~Entrada[3], ~Entrada[2], Entrada[1]);  // AND_Gate
  and and_10 (and_10_out, ~Entrada[2], ~Entrada[0]);  // AND_Gate
  and and_11 (and_11_out, Entrada[1], ~Entrada[0]);  // AND_Gate
  and and_12 (and_12_out, ~Entrada[1], ~Entrada[0]);  // AND_Gate
  and and_13 (and_13_out, ~Entrada[3], Entrada[2], ~Entrada[1]);  // AND_Gate
  and and_14 (and_14_out, ~Entrada[3], Entrada[2], ~Entrada[0]);  // AND_Gate
  and and_15 (and_15_out, Entrada[2], ~Entrada[1]);  // AND_Gate
  and and_16 (and_16_out, ~Entrada[2], Entrada[1]);  // AND_Gate
  and and_17 (and_17_out, Entrada[1], ~Entrada[0]);  // AND_Gate
  or or_1 (fa, Entrada[3], and_1_out, and_2_out, Entrada[1]);
  or or_2 (fb, ~Entrada[2], and_3_out, and_4_out);  // OR_Gate
  or or_3 (fc, Entrada[2], ~Entrada[1], and_5_out);  // OR_Gate
  or or_4 (fd, Entrada[3], and_6_out, and_7_out, and_8_out, and_9_out);
  or or_5 (fe, and_10_out, and_11_out);
  or or_6 (ff, Entrada[3], and_12_out, and_13_out, and_14_out);
  or or_7 (fg, Entrada[3], and_15_out, and_16_out, and_17_out);

  // Notes on the sheet:
  //   w
  //   x
  //   y
  //   z
endmodule

module count_hits (
  input  Reset,
  input  clock,
  output [5:0] Count_value
);

  Counter #(.max('h3f), .width(6)) counter_1 (
    .clr(Reset), .up(1'b1), .count(1'b1), .clk(clock), .Q(Count_value));  // open: load, D, carry
  // Probe on Count_value
endmodule

module count_fails (
  input  Reset,
  input  CLK,
  output Fin,
  output [3:0] Count_value
);

  wire and_1_out;

  and and_1 (and_1_out, Count_value[1], Count_value[0]);
  J_K_Flip_Flop J3K3 (.Q(Count_value[3]));  // open: J, clk, K, Qn, preset, reset
  J_K_Flip_Flop J2K2 (.J(and_1_out), .clk(CLK), .K(and_1_out), .Q(Count_value[2]), .reset(Reset));  // open: Qn, preset
  J_K_Flip_Flop J1K1 (
    .J(Count_value[0]), .clk(CLK), .K(Count_value[0]), .Q(Count_value[1]), .reset(Reset));  // open: Qn, preset
  J_K_Flip_Flop J0K0 (.J(1'b1), .clk(CLK), .K(1'b1), .Q(Count_value[0]), .reset(Reset));  // open: Qn, preset
  and and_2 (Fin, Count_value[2], Count_value[1], Count_value[0]);
  // Probe on Count_value

  // Other names for the same wires on the sheet: r = CLK; s = Reset
endmodule

module stars_fall (
  input  Reset,
  input  Clock,
  input  [15:0] Down,
  output [15:0] R1,
  output [15:0] R2,
  output [15:0] R3,
  output [15:0] R4,
  output [15:0] R5,
  output [15:0] R6,
  output [15:0] R7,
  output [15:0] R8,
  output [15:0] R9,
  output [15:0] R10,
  output [15:0] R11,
  output [15:0] R12,
  output [15:0] R13,
  output [15:0] R14,
  output [15:0] R15
);

  // Shift_Register #(.length(15), .width(16)) shift_register_1: pin names not known; wires that end beside it: Reset, Clock, Down, R1, R2, R3, R4, R5, R6, R7, R8, R9, R10, R11, R12
endmodule

module Comparador (
  input  [15:0] R15,
  input  [15:0] cursor,
  output Hit,
  output Fail
);

  wire comparator_2_eq, not_1_out, not_2_out;

  Comparator #(.width(16)) comparator_1 (.a(R15), .b(cursor), .eq(Hit));  // open: gt, lt
  not not_1 (not_1_out, comparator_2_eq);
  Comparator #(.width(16)) comparator_2 (.a(R15), .b({16{1'b0}}), .eq(comparator_2_eq));  // open: gt, lt
  not not_2 (not_2_out, Hit);
  and and_1 (Fail, not_2_out, not_1_out);
endmodule

module random_num (
  input  Reset,
  input  Clock,
  output [3:0] Num_random
);

  // Random #(.width(4)) random_1: pin names not known; wires that end beside it: Clock, Reset
  // Probe on Num_random
endmodule

module mod2 (
  input  Clock,
  output Value
);

  J_K_Flip_Flop j_k_ff_1 (.J(1'b1), .clk(Clock), .K(1'b1), .Q(Value));  // open: Qn, preset, reset
endmodule

module Driver (
  input  [3:0] input1,
  output [15:0] out_2
);

  Decoder #(.select(4)) decoder_1 (
    .out0(out_2[0]), .out1(out_2[1]), .out2(out_2[2]), .out3(out_2[3]), .out4(out_2[4]), .out5(out_2[5]),
    .out6(out_2[6]), .out7(out_2[7]), .out8(out_2[8]), .out9(out_2[9]), .out10(out_2[10]), .out11(out_2[11]),
    .out12(out_2[12]), .out13(out_2[13]), .out14(out_2[14]), .out15(out_2[15]), .sel(input1));  // open: en
endmodule

module ensayos (
  output [15:0] out1
);

  wire [3:0] undriven;
  wire [15:0] and_1_out;

  and and_1 (and_1_out[0], ~undriven[0], ~undriven[1], ~undriven[3], ~undriven[3]);  // AND_Gate
  and and_2 (and_1_out[1], undriven[0], ~undriven[1], ~undriven[3], ~undriven[3]);  // AND_Gate
  and and_3 (and_1_out[2], undriven[1], ~undriven[0], ~undriven[3], ~undriven[3]);  // AND_Gate
  and and_4 (and_1_out[3], undriven[0], undriven[1], ~undriven[3], ~undriven[3]);  // AND_Gate
  and and_5 (and_1_out[4], undriven[3], ~undriven[0], ~undriven[1], ~undriven[3]);  // AND_Gate
  and and_6 (and_1_out[5], undriven[0], undriven[3], ~undriven[1], ~undriven[3]);  // AND_Gate
  and and_7 (and_1_out[6], undriven[1], undriven[3], ~undriven[0], ~undriven[3]);  // AND_Gate
  and and_8 (and_1_out[7], undriven[0], undriven[1], undriven[3], ~undriven[3]);  // AND_Gate
  and and_9 (and_1_out[8], undriven[3], ~undriven[3], ~undriven[1], ~undriven[0]);  // AND_Gate
  and and_10 (and_1_out[9], undriven[3], undriven[0], ~undriven[1], ~undriven[3]);  // AND_Gate
  and and_11 (and_1_out[10], ~undriven[0], undriven[1], ~undriven[3], undriven[3]);  // AND_Gate
  and and_12 (and_1_out[11], undriven[0], undriven[1], ~undriven[3], undriven[3]);  // AND_Gate
  and and_13 (and_1_out[12], ~undriven[0], ~undriven[1], undriven[3], undriven[3]);  // AND_Gate
  and and_14 (and_1_out[13], undriven[0], ~undriven[1], undriven[3], undriven[3]);  // AND_Gate
  and and_15 (and_1_out[14], ~undriven[0], undriven[1], undriven[3], undriven[3]);  // AND_Gate
  and and_16 (and_1_out[15], undriven[0], undriven[1], undriven[3], undriven[3]);
  // Probe on nothing

  // Notes on the sheet:
  //   w
  //   x
  //   y
  //   z
endmodule

module frecuencias (
  input  nvl2,
  input  nvl1,
  input  CLK,
  output salida
);

  wire CLK2, CLK4;

  divisor_reloj_frecuency divisor_reloj_frecuency_1 (
    .nivel1(nvl1), .nivel2(nvl2), .Clock(CLK), .CLKD2(CLK2), .CLKD4(CLK4));  // open: reset, CLKD8
  or or_1 (salida, CLK2, CLK4);
endmodule
